// Digital circuit CPU.dig as structural Verilog
module CPU (
  input  RST,
  input  CLK,
  input  clk_2,
  input  CLK_SEL,
  input  EXTERNAL_BUTTON,
  output [7:0] opcode,
  output [15:0] rom
);

  wire A_LD, A_OE, A_SEL, addressdecoder_1_nram_cs, addressdecoder_1_nrom_cs, alu_1_c_flag, alu_1_n_flag,
       alu_1_v_flag, alu_1_z_flag, ALU_CIN, ALU_S0, ALU_S1, ALU_S2, and_1_out, and_2_out, B_SET, C, CLK_t,
       FL_SEL, I, I_SET, I_WRITE, irq_latch_1_p5, MAR_DIR, MEM_RD, MEM_WR, N, nALU_OE, nCLR_IRQ, nFL_LD,
       nFL_OE, nHBA_OE, nIR_LD, nIRA_OE, nIRD_OE, nMAR_INC, nMAR_OE, nMARH_LD, nMARL_LD, nMPC_RST, not_1_out,
       nPC_LD, nPCH_OE, nPCL_OE, nRST, nSHR, nSP_INC, nSP_LD, nSP_OE, nSPH_OE, nSPL_OE, nV_OE, nXY_AOE,
       nXY_INC, PC_INC, PC_OE, REG_LD, REG_OE, SHR_IN0, SP_DIR, V, V_B0, XY_DIR, Z;
  wire [2:0] micropc_1_microstep, Rsrc;
  wire [7:0] int_vect_1_p3, int_vect_1_p3_2, sp_a_1_d_out;
  wire [15:0] pc_1_p6;
  wire [15:13] ctrlunit_1_c32_47;

  // INT_VECT int_vect_1: pin names not known; wires that end beside it: nV_OE, V_B0, {int_vect_1_p3, int_vect_1_p3_2}
  not not_1 (not_1_out, RST);
  // A_H__BUFFER a_h__buffer_1: pin names not known; wires that end beside it: nHBA_OE
  ADDRESSDECODER addressdecoder_1 (
    .A_BUS({int_vect_1_p3, int_vect_1_p3_2}), .nRAM_CS(addressdecoder_1_nram_cs),
    .nROM_CS(addressdecoder_1_nrom_cs));  // open: nFB_CS, nMMIO_CS
  not not_2 (nRST, RST);
  // RST_Buffer rst_buffer_1: pin names not known; wires that end beside it: not_1_out, int_vect_1_p3, {int_vect_1_p3, int_vect_1_p3_2}
  and and_1 (and_1_out, CLK, ~CLK_SEL);  // And
  and and_2 (and_2_out, CLK_SEL, clk_2);
  or or_1 (CLK_t, and_1_out, and_2_out);
  // PC pc_1: pin names not known; wires that end beside it: {int_vect_1_p3, int_vect_1_p3_2}, PC_INC, nPC_LD, CLK_t, RST, pc_1_p6
  SP_a sp_a_1 (
    .A_IN({int_vect_1_p3, int_vect_1_p3_2}), .nSP_INC(nSP_INC), .SP_DIR(SP_DIR), .nSP_LD(nSP_LD),
    .nSP_OE(nSP_OE), .nSPH_OE(nSPH_OE), .nSPL_OE(nSPL_OE), .CLK(CLK_t),
    .A_OUT({int_vect_1_p3, int_vect_1_p3_2}), .D_OUT(sp_a_1_d_out));
  // MAR mar_1: pin names not known; wires that end beside it: {int_vect_1_p3, int_vect_1_p3_2}, CLK_t, MAR_DIR, nMAR_INC, nMAR_OE, nMARH_LD, nMARL_LD, sp_a_1_d_out
  RAMSinglePortSel #(.AddrBits(16), .Bits(8)) ramsingleportsel_1 (
    .A({int_vect_1_p3, int_vect_1_p3_2}), .CS(~addressdecoder_1_nram_cs), .WE(MEM_WR), .OE(MEM_RD),
    .D(sp_a_1_d_out));
  EEPROM #(.AddrBits(15), .Bits(16)) eeprom_1 (
    .A({1'b0, int_vect_1_p3[5:0], int_vect_1_p3_2}), .CS(~addressdecoder_1_nrom_cs), .WE(1'b0), .OE(MEM_RD),
    .D(rom));
  PC_BUFFER pc_buffer_1 (
    .PC(pc_1_p6), .PC_OE(PC_OE), .nPCH_OE(nPCH_OE), .nPCL_OE(nPCL_OE), .RST(RST),
    .A_BUS({int_vect_1_p3, int_vect_1_p3_2}), .D_BUS(sp_a_1_d_out));
  IR ir_1 (
    .ROM_IN(rom), .nIR_LD(nIR_LD), .nIRD_OE(nIRD_OE), .nIRA_OE(nIRA_OE), .CLK(CLK_t), ._15_11(opcode[7:3]),
    ._10_8(opcode[2:0]), ._7_5(Rsrc), ._0_7(sp_a_1_d_out), .AB(int_vect_1_p3_2));
  microPC micropc_1 (.CLK(CLK_t), .nMPC_RST(nMPC_RST), .microstep(micropc_1_microstep));
  // IRQ_LATCH irq_latch_1: pin names not known; wires that end beside it: EXTERNAL_BUTTON, I, nCLR_IRQ, nMPC_RST, irq_latch_1_p5
  // RFILE rfile_1: pin names not known; wires that end beside it: sp_a_1_d_out, opcode[2:0], Rsrc, REG_LD, REG_OE, nXY_INC, XY_DIR, nXY_AOE, CLK_t, RST, sp_a_1_d_out, {int_vect_1_p3, int_vect_1_p3_2}, A_LD, A_OE
  ALU alu_1 (
    .DATA(sp_a_1_d_out), .A_LD(A_LD), .A_OE(A_OE), .A_SEL(A_SEL), .ALU_S0(ALU_S0), .ALU_S1(ALU_S1),
    .ALU_S2(ALU_S2), .nALU_OE(nALU_OE), .ALU_CIN(ALU_CIN), .nSHR(nSHR), .SHR_IN0(SHR_IN0), .CLK(CLK_t),
    .RST(RST), .DATA_2(sp_a_1_d_out), .Z_FLAG(alu_1_z_flag), .C_FLAG(alu_1_c_flag), .N_FLAG(alu_1_n_flag),
    .V_FLAG(alu_1_v_flag));
  CTRLUNIT ctrlunit_1 (
    .OPC(opcode), .microstep(micropc_1_microstep), .Z(Z), .C(C), .N(N), .V(V), .IRQ(irq_latch_1_p5),
    .C0_15({nMAR_INC, nMAR_OE, nMARH_LD, nMARL_LD, MEM_WR, MEM_RD, nMPC_RST, nHBA_OE, nIRA_OE, nIRD_OE, nIR_LD, nPCH_OE, nPCL_OE, PC_OE, nPC_LD, PC_INC}),
    .C16_31({nFL_LD, nFL_OE, SHR_IN0, nSHR, ALU_CIN, nALU_OE, ALU_S2, ALU_S1, ALU_S0, A_SEL, nXY_AOE, XY_DIR, nXY_INC, REG_OE, REG_LD, MAR_DIR}),
    .C32_47({ctrlunit_1_c32_47, V_B0, nV_OE, nCLR_IRQ, nSPH_OE, nSPL_OE, nSP_OE, nSP_LD, SP_DIR, nSP_INC, I_WRITE, I_SET, B_SET, FL_SEL}));
  FLAG_REG flag_reg_1 (
    .D_IN(sp_a_1_d_out), .Z_FLAG(alu_1_z_flag), .C_FLAG(alu_1_c_flag), .N_FLAG(alu_1_n_flag),
    .V_FLAG(alu_1_v_flag), .I_SET(I_SET), .I_WRITE(I_WRITE), .nFL_OE(B_SET), .nFL_LD(nFL_OE),
    .FL_SEL(nFL_LD), .FB(FL_SEL), .CLK(CLK_t), .nRST(nRST), .D_OUT(sp_a_1_d_out), .Z(Z), .C(C), .N(N), .V(V),
    .I(I));

  // Other names for the same wires on the sheet: Rdst[2:0] = opcode[2:0]

  // Notes on the sheet:
  //   clk_2: Hz: 10
  //   contents of eeprom_1 (hex, n*v repeats v):
  //   fd00,63f,7ff,f200,1009,11c0,ea00,610,710,20,6810,900,fb00
endmodule
