// Digital circuit CTRLUNIT.dig as structural Verilog
module CTRLUNIT (
  input  [7:0] OPC,
  input  [2:0] microstep,
  input  Z,
  input  C,
  input  N,
  input  V,
  input  I,
  output [15:0] C0_15,
  output [15:0] C16_31,
  output [15:0] C32_47
);

  ROM #(.AddrBits(16), .Bits(16)) _1ROM (.A({I, V, N, C, Z, microstep, OPC}), .sel(1'b1), .D(C0_15));
  ROM #(.AddrBits(16), .Bits(16)) _2ROM (.A({I, V, N, C, Z, microstep, OPC}), .sel(1'b1), .D(C16_31));
  ROM #(.AddrBits(16), .Bits(16)) _3ROM (.A({I, V, N, C, Z, microstep, OPC}), .sel(1'b1), .D(C32_47));

  // Notes on the sheet:
  //   contents of _1ROM (hex, n*v repeats v):
  //   256*77da,8*f1bb,8*f1fb,61bb,61bb,6*73fb,61fb,61fb,6*73fb,8*f47f
  //   ,8*b5ff,8*f5ff,8*787f,8*39ff,16*79ff,8*f5ff,8*f1fb,8*f1bb,32*f1fb
  //   ,8*f1bb,16*f1fb,16*f1bb,16*f1fb,8*71fb,8*71bb,31fd,71fb,5*73fb
  //   ,31fd,7*73fb,71fd,79f7,71fb,6*7bf7,73fb,63fb,73fb,71fb,71fb,73fb
  //   ,f1fb,f1fb,71fb,71fb,73fb,57ff,73fb,71fb,71fb,73fb,240*73fa,31fe
  //   ,51fa,71fe,5*73fa,71fa,71fa,73fa,73fa,73fa,71fa,71fa,249*73fa
  //   ,71fa,71fa,73fa,73fa,73fa,71fa,71fa,249*73fa,71fa,71fa,73fa,73fa,73fa
  //   ,71fa,71fa,249*73fa,71fa,71fa,73fa,73fa,73fa,71fa,71fa,249*73fa
  //   ,71fa,71fa,73fa,73fa,73fa,71fa,71fa,249*73fa,71fa,71fa,73fa,73fa,73fa
  //   ,71fa,71fa,73fa,256*77da,8*f1bb,8*f1fb,61bb,61bb,6*73fb,61fb,61fb
  //   ,6*73fb,8*f47f,8*b5ff,8*f5ff,8*787f,8*39ff,16*79ff,8*f5ff,8*f1fb
  //   ,8*f1bb,32*f1fb,8*f1bb,16*f1fb,16*f1bb,16*f1fb,8*71fb,8*71bb,31fd
  //   ,71fb,5*73fb,31fd,7*73fb,71fd,79f7,71fb,6*7bf7,73fb,63fb,73fb
  //   ,71fb,71fb,73fb,f1fb,f1fb,71fb,71fb,73fb,57ff,73fb,71fb,71fb,73fb
  //   ,240*73fa,31fe,51fa,71fe,5*73fa,71fa,71fa,73fa,73fa,73fa,71fa,71fa
  //   ,249*73fa,71fa,71fa,73fa,73fa,73fa,71fa,71fa,249*73fa,71fa,71fa
  //   ,73fa,73fa,73fa,71fa,71fa,249*73fa,71fa,71fa,73fa,73fa,73fa,71fa,71fa
  //   ,249*73fa,71fa,71fa,73fa,73fa,73fa,71fa,71fa,249*73fa,71fa,71fa
  //   ,73fa,73fa,73fa,71fa,71fa,73fa,256*77da,8*f1bb,8*f1fb,61bb,61bb
  //   ,6*73fb,61fb,61fb,6*73fb,8*f47f,8*b5ff,8*f5ff,8*787f,8*39ff,16*79ff
  //   ,8*f5ff,8*f1fb,8*f1bb,32*f1fb,8*f1bb,16*f1fb,16*f1bb,16*f1fb,8*71fb
  //   ,8*71bb,31fd,71fb,5*73fb,31fd,7*73fb,71fd,79f7,71fb,6*7bf7,73fb
  //   ,63fb,73fb,71fb,71fb,73fb,f1fb,f1fb,71fb,71fb,73fb,57ff,73fb,71fb,71fb
  //   ,73fb,240*73fa,31fe,51fa,71fe,5*73fa,71fa,71fa,73fa,73fa,73fa
  //   ,71fa,71fa,249*73fa,71fa,71fa,73fa,73fa,73fa,71fa,71fa,249*73fa
  //   ,71fa,71fa,73fa,73fa,73fa,71fa,71fa,249*73fa,71fa,71fa,73fa,73fa,73fa
  //   ,71fa,71fa,249*73fa,71fa,71fa,73fa,73fa,73fa,71fa,71fa,249*73fa
  //   ,71fa,71fa,73fa,73fa,73fa,71fa,71fa,73fa,256*77da,8*f1bb,8*f1fb
  //   ,61bb,61bb,6*73fb,61fb,61fb,6*73fb,8*f47f,8*b5ff,8*f5ff,8*787f
  //   ,8*39ff,16*79ff,8*f5ff,8*f1fb,8*f1bb,32*f1fb,8*f1bb,16*f1fb,16*f1bb
  //   ,16*f1fb,8*71fb,8*71bb,31fd,71fb,5*73fb,31fd,7*73fb,71fd,79f7
  //   ,71fb,6*7bf7,73fb,63fb,73fb,71fb,71fb,73fb,f1fb,f1fb,71fb,71fb
  //   ,73fb,57ff,73fb,71fb,71fb,73fb,240*73fa,31fe,51fa,71fe,5*73fa
  //   ,71fa,71fa,73fa,73fa,73fa,71fa,71fa,249*73fa,71fa,71fa,73fa,73fa,73fa
  //   ,71fa,71fa,249*73fa,71fa,71fa,73fa,73fa,73fa,71fa,71fa,249*73fa
  //   ,71fa,71fa,73fa,73fa,73fa,71fa,71fa,249*73fa,71fa,71fa,73fa,73fa,73fa
  //   ,71fa,71fa,249*73fa,71fa,71fa,73fa,73fa,73fa,71fa,71fa,73fa,256*77da
  //   ,8*f1bb,8*f1fb,61bb,61bb,6*73fb,61fb,61fb,6*73fb,8*f47f,8*b5ff
  //   ,8*f5ff,8*787f,8*39ff,16*79ff,8*f5ff,8*f1fb,8*f1bb,32*f1fb,8*f1bb
  //   ,16*f1fb,16*f1bb,16*f1fb,8*71fb,8*71bb,31fd,71fb,5*73fb,31fd,7*73fb
  //   ,71fd,79f7,71fb,6*7bf7,73fb,63fb,73fb,71fb,71fb,73fb,f1fb,f1fb
  //   ,71fb,71fb,73fb,57ff,73fb,71fb,71fb,73fb,240*73fa,31fe,51fa,71fe
  //   ,5*73fa,71fa,71fa,73fa,73fa,73fa,71fa,71fa,249*73fa,71fa,71fa
  //   ,73fa,73fa,73fa,71fa,71fa,249*73fa,71fa,71fa,73fa,73fa,73fa,71fa,71fa
  //   ,249*73fa,71fa,71fa,73fa,73fa,73fa,71fa,71fa,249*73fa,71fa,71fa
  //   ,73fa,73fa,73fa,71fa,71fa,249*73fa,71fa,71fa,73fa,73fa,73fa,71fa,71fa
  //   ,73fa,256*77da,8*f1bb,8*f1fb,61bb,61bb,6*73fb,61fb,61fb,6*73fb
  //   ,8*f47f,8*b5ff,8*f5ff,8*787f,8*39ff,16*79ff,8*f5ff,8*f1fb,8*f1bb
  //   ,32*f1fb,8*f1bb,16*f1fb,16*f1bb,16*f1fb,8*71fb,8*71bb,31fd,71fb
  //   ,5*73fb,31fd,7*73fb,71fd,79f7,71fb,6*7bf7,73fb,63fb,73fb,71fb,71fb
  //   ,73fb,f1fb,f1fb,71fb,71fb,73fb,57ff,73fb,71fb,71fb,73fb,240*73fa
  //   ,31fe,51fa,71fe,5*73fa,71fa,71fa,73fa,73fa,73fa,71fa,71fa,249*73fa
  //   ,71fa,71fa,73fa,73fa,73fa,71fa,71fa,249*73fa,71fa,71fa,73fa,73fa,73fa
  //   ,71fa,71fa,249*73fa,71fa,71fa,73fa,73fa,73fa,71fa,71fa,249*73fa
  //   ,71fa,71fa,73fa,73fa,73fa,71fa,71fa,249*73fa,71fa,71fa,73fa,73fa,73fa
  //   ,71fa,71fa,73fa,256*77da,8*f1bb,8*f1fb,61bb,61bb,6*73fb,61fb,61fb
  //   ,6*73fb,8*f47f,8*b5ff,8*f5ff,8*787f,8*39ff,16*79ff,8*f5ff,8*f1fb
  //   ,8*f1bb,32*f1fb,8*f1bb,16*f1fb,16*f1bb,16*f1fb,8*71fb,8*71bb,31fd
  //   ,71fb,5*73fb,31fd,7*73fb,71fd,79f7,71fb,6*7bf7,73fb,63fb,73fb
  //   ,71fb,71fb,73fb,f1fb,f1fb,71fb,71fb,73fb,57ff,73fb,71fb,71fb,73fb
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  //   contents of _2ROM (hex, n*v repeats v):
  //   264*350a,8*350b,8*350a,350b,350b,22*350a,8*3502,16*350b,8*3503
  //   ,8*350b,8*350a,8*157b,8*157a,8*177b,8*175b,8*155b,8*15db,8*15da
  //   ,8*15bb,8*159b,8*177a,8*155a,16*310a,8*174b,8*174a,15*350a,3502
  //   ,3508,350c,264*350a,3502,1557*350a,8*350b,8*350a,350b,350b,22*350a
  //   ,8*3502,16*350b,8*3503,8*350b,8*350a,8*157b,8*157a,8*177b,8*175b
  //   ,8*155b,8*15db,8*15da,8*15bb,8*159b,8*177a,8*155a,16*310a,8*174b
  //   ,8*174a,15*350a,3502,3508,350c,264*350a,3502,1557*350a,8*350b
  //   ,8*350a,350b,350b,22*350a,8*3502,16*350b,8*3503,8*350b,8*350a
  //   ,8*157b,8*157a,8*177b,8*175b,8*155b,8*15db,8*15da,8*15bb,8*159b
  //   ,8*177a,8*155a,16*310a,8*174b,8*174a,15*350a,3502,3508,350c,264*350a
  //   ,3502,1557*350a,8*350b,8*350a,350b,350b,22*350a,8*3502,16*350b
  //   ,8*3503,8*350b,8*350a,8*157b,8*157a,8*177b,8*175b,8*155b,8*15db
  //   ,8*15da,8*15bb,8*159b,8*177a,8*155a,16*310a,8*174b,8*174a,15*350a
  //   ,3502,3508,350c,264*350a,3502,1557*350a,8*350b,8*350a,350b,350b
  //   ,22*350a,8*3502,16*350b,8*3503,8*350b,8*350a,8*157b,8*157a,8*177b
  //   ,8*175b,8*155b,8*15db,8*15da,8*15bb,8*159b,8*177a,8*155a,16*310a
  //   ,8*174b,8*174a,15*350a,3502,3508,350c,264*350a,3502,1557*350a
  //   ,8*350b,8*350a,350b,350b,22*350a,8*3502,16*350b,8*3503,8*350b
  //   ,8*350a,8*157b,8*157a,8*177b,8*175b,8*155b,8*15db,8*15da,8*15bb
  //   ,8*159b,8*177a,8*155a,16*310a,8*174b,8*174a,15*350a,3502,3508
  //   ,350c,264*350a,3502,1557*350a,8*350b,8*350a,350b,350b,22*350a
  //   ,8*3502,16*350b,8*3503,8*350b,8*350a,8*157b,8*157a,8*177b,8*175b
  //   ,8*155b,8*15db,8*15da,8*15bb,8*159b,8*177a,8*155a,16*310a,8*174b
  //   ,8*174a,15*350a,3502,3508,350c,264*350a,3502,1557*350a,8*350b
  //   ,8*350a,350b,350b,22*350a,8*3502,16*350b,8*3503,8*350b,8*350a
  //   ,8*157b,8*157a,8*177b,8*175b,8*155b,8*15db,8*15da,8*15bb,8*159b
  //   ,8*177a,8*155a,16*310a,8*174b,8*174a,15*350a,3502,3508,350c,264*350a
  //   ,3502,1557*350a,8*350b,8*350a,350b,350b,22*350a,8*3502,16*350b
  //   ,8*3503,8*350b,8*350a,8*157b,8*157a,8*177b,8*175b,8*155b,8*15db
  //   ,8*15da,8*15bb,8*159b,8*177a,8*155a,16*310a,8*174b,8*174a,15*350a
  //   ,3502,3508,350c,264*350a,3502,1557*350a,8*350b,8*350a,350b,350b
  //   ,22*350a,8*3502,16*350b,8*3503,8*350b,8*350a,8*157b,8*157a,8*177b
  //   ,8*175b,8*155b,8*15db,8*15da,8*15bb,8*159b,8*177a,8*155a,16*310a
  //   ,8*174b,8*174a,15*350a,3502,3508,350c,264*350a,3502,1557*350a
  //   ,8*350b,8*350a,350b,350b,22*350a,8*3502,16*350b,8*3503,8*350b
  //   ,8*350a,8*157b,8*157a,8*177b,8*175b,8*155b,8*15db,8*15da,8*15bb
  //   ,8*159b,8*177a,8*155a,16*310a,8*174b,8*174a,15*350a,3502,3508
  //   ,350c,264*350a,3502,1557*350a,8*350b,8*350a,350b,350b,22*350a
  //   ,8*3502,16*350b,8*3503,8*350b,8*350a,8*157b,8*157a,8*177b,8*175b
  //   ,8*155b,8*15db,8*15da,8*15bb,8*159b,8*177a,8*155a,16*310a,8*174b
  //   ,8*174a,15*350a,3502,3508,350c,264*350a,3502,1557*350a,8*350b
  //   ,8*350a,350b,350b,22*350a,8*3502,16*350b,8*3503,8*350b,8*350a
  //   ,8*157b,8*157a,8*177b,8*175b,8*155b,8*15db,8*15da,8*15bb,8*159b
  //   ,8*177a,8*155a,16*310a,8*174b,8*174a,15*350a,3502,3508,350c,264*350a
  //   ,3502,1557*350a,8*350b,8*350a,350b,350b,22*350a,8*3502,16*350b
  //   ,8*3503,8*350b,8*350a,8*157b,8*157a,8*177b,8*175b,8*155b,8*15db
  //   ,8*15da,8*15bb,8*159b,8*177a,8*155a,16*310a,8*174b,8*174a,15*350a
  //   ,3502,3508,350c,264*350a,3502,1557*350a,8*350b,8*350a,350b,350b
  //   ,22*350a,8*3502,16*350b,8*3503,8*350b,8*350a,8*157b,8*157a,8*177b
  //   ,8*175b,8*155b,8*15db,8*15da,8*15bb,8*159b,8*177a,8*155a,16*310a
  //   ,8*174b,8*174a,15*350a,3502,3508,350c,264*350a,3502,1557*350a
  //   ,8*350b,8*350a,350b,350b,22*350a,8*3502,16*350b,8*3503,8*350b
  //   ,8*350a,8*157b,8*157a,8*177b,8*175b,8*155b,8*15db,8*15da,8*15bb
  //   ,8*159b,8*177a,8*155a,16*310a,8*174b,8*174a,15*350a,3502,3508
  //   ,350c,264*350a,3502,1557*350a,8*350b,8*350a,350b,350b,22*350a
  //   ,8*3502,16*350b,8*3503,8*350b,8*350a,8*157b,8*157a,8*177b,8*175b
  //   ,8*155b,8*15db,8*15da,8*15bb,8*159b,8*177a,8*155a,16*310a,8*174b
  //   ,8*174a,15*350a,3502,3508,350c,264*350a,3502,1557*350a,8*350b
  //   ,8*350a,350b,350b,22*350a,8*3502,16*350b,8*3503,8*350b,8*350a
  //   ,8*157b,8*157a,8*177b,8*175b,8*155b,8*15db,8*15da,8*15bb,8*159b
  //   ,8*177a,8*155a,16*310a,8*174b,8*174a,15*350a,3502,3508,350c,264*350a
  //   ,3502,1557*350a,8*350b,8*350a,350b,350b,22*350a,8*3502,16*350b
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  //   contents of _3ROM (hex, n*v repeats v):
  //   336*f4,8*d8,8*d0,136*f4,d8,f4,6*d8,f4,b4,f4,f0,f8,f4,74,b4,f4,f4,f4
  //   ,d0,f4,f7,f6,241*f4,e4,74,e4,10*f4,f7,f6,254*f4,f7,f6,254*f4,f7
  //   ,f6,254*f4,f7,f6,254*f4,f7,f6,254*f4,f7,f6,337*f4,8*d8,8*d0,136*f4
  //   ,d8,f4,6*d8,f4,b4,f4,f0,f8,f4,74,b4,f4,f4,f4,d0,f4,f7,f6,241*f4
  //   ,e4,74,e4,10*f4,f7,f6,254*f4,f7,f6,254*f4,f7,f6,254*f4,f7,f6,254*f4
  //   ,f7,f6,254*f4,f7,f6,337*f4,8*d8,8*d0,136*f4,d8,f4,6*d8,f4,b4,f4
  //   ,f0,f8,f4,74,b4,f4,f4,f4,d0,f4,f7,f6,241*f4,e4,74,e4,10*f4,f7
  //   ,f6,254*f4,f7,f6,254*f4,f7,f6,254*f4,f7,f6,254*f4,f7,f6,254*f4
  //   ,f7,f6,337*f4,8*d8,8*d0,136*f4,d8,f4,6*d8,f4,b4,f4,f0,f8,f4,74
  //   ,b4,f4,f4,f4,d0,f4,f7,f6,241*f4,e4,74,e4,10*f4,f7,f6,254*f4,f7
  //   ,f6,254*f4,f7,f6,254*f4,f7,f6,254*f4,f7,f6,254*f4,f7,f6,337*f4
  //   ,8*d8,8*d0,136*f4,d8,f4,6*d8,f4,b4,f4,f0,f8,f4,74,b4,f4,f4,f4
  //   ,d0,f4,f7,f6,241*f4,e4,74,e4,10*f4,f7,f6,254*f4,f7,f6,254*f4,f7
  //   ,f6,254*f4,f7,f6,254*f4,f7,f6,254*f4,f7,f6,337*f4,8*d8,8*d0,136*f4
  //   ,d8,f4,6*d8,f4,b4,f4,f0,f8,f4,74,b4,f4,f4,f4,d0,f4,f7,f6,241*f4
  //   ,e4,74,e4,10*f4,f7,f6,254*f4,f7,f6,254*f4,f7,f6,254*f4,f7,f6,254*f4
  //   ,f7,f6,254*f4,f7,f6,337*f4,8*d8,8*d0,136*f4,d8,f4,6*d8,f4,b4,f4
  //   ,f0,f8,f4,74,b4,f4,f4,f4,d0,f4,f7,f6,241*f4,e4,74,e4,10*f4,f7
  //   ,f6,254*f4,f7,f6,254*f4,f7,f6,254*f4,f7,f6,254*f4,f7,f6,254*f4
  //   ,f7,f6,337*f4,8*d8,8*d0,136*f4,d8,f4,6*d8,f4,b4,f4,f0,f8,f4,74
  //   ,b4,f4,f4,f4,d0,f4,f7,f6,241*f4,e4,74,e4,10*f4,f7,f6,254*f4,f7
  //   ,f6,254*f4,f7,f6,254*f4,f7,f6,254*f4,f7,f6,254*f4,f7,f6,337*f4
  //   ,8*d8,8*d0,136*f4,d8,f4,6*d8,f4,b4,f4,f0,f8,f4,74,b4,f4,f4,f4
  //   ,d0,f4,f7,f6,241*f4,e4,74,e4,10*f4,f7,f6,254*f4,f7,f6,254*f4,f7
  //   ,f6,254*f4,f7,f6,254*f4,f7,f6,254*f4,f7,f6,337*f4,8*d8,8*d0,136*f4
  //   ,d8,f4,6*d8,f4,b4,f4,f0,f8,f4,74,b4,f4,f4,f4,d0,f4,f7,f6,241*f4
  //   ,e4,74,e4,10*f4,f7,f6,254*f4,f7,f6,254*f4,f7,f6,254*f4,f7,f6,254*f4
  //   ,f7,f6,254*f4,f7,f6,337*f4,8*d8,8*d0,136*f4,d8,f4,6*d8,f4,b4,f4
  //   ,f0,f8,f4,74,b4,f4,f4,f4,d0,f4,f7,f6,241*f4,e4,74,e4,10*f4,f7
  //   ,f6,254*f4,f7,f6,254*f4,f7,f6,254*f4,f7,f6,254*f4,f7,f6,254*f4
  //   ,f7,f6,337*f4,8*d8,8*d0,136*f4,d8,f4,6*d8,f4,b4,f4,f0,f8,f4,74
  //   ,b4,f4,f4,f4,d0,f4,f7,f6,241*f4,e4,74,e4,10*f4,f7,f6,254*f4,f7
  //   ,f6,254*f4,f7,f6,254*f4,f7,f6,254*f4,f7,f6,254*f4,f7,f6,337*f4
  //   ,8*d8,8*d0,136*f4,d8,f4,6*d8,f4,b4,f4,f0,f8,f4,74,b4,f4,f4,f4
  //   ,d0,f4,f7,f6,241*f4,e4,74,e4,10*f4,f7,f6,254*f4,f7,f6,254*f4,f7
  //   ,f6,254*f4,f7,f6,254*f4,f7,f6,254*f4,f7,f6,337*f4,8*d8,8*d0,136*f4
  //   ,d8,f4,6*d8,f4,b4,f4,f0,f8,f4,74,b4,f4,f4,f4,d0,f4,f7,f6,241*f4
  //   ,e4,74,e4,10*f4,f7,f6,254*f4,f7,f6,254*f4,f7,f6,254*f4,f7,f6,254*f4
  //   ,f7,f6,254*f4,f7,f6,337*f4,8*d8,8*d0,136*f4,d8,f4,6*d8,f4,b4,f4
  //   ,f0,f8,f4,74,b4,f4,f4,f4,d0,f4,f7,f6,241*f4,e4,74,e4,10*f4,f7
  //   ,f6,254*f4,f7,f6,254*f4,f7,f6,254*f4,f7,f6,254*f4,f7,f6,254*f4
  //   ,f7,f6,337*f4,8*d8,8*d0,136*f4,d8,f4,6*d8,f4,b4,f4,f0,f8,f4,74
  //   ,b4,f4,f4,f4,d0,f4,f7,f6,241*f4,e4,74,e4,10*f4,f7,f6,254*f4,f7
  //   ,f6,254*f4,f7,f6,254*f4,f7,f6,254*f4,f7,f6,254*f4,f7,f6,337*f4
  //   ,8*d8,8*d0,136*f4,d8,f4,6*d8,f4,b4,f4,f0,f8,f4,74,b4,f4,f4,f4
  //   ,d0,f4,f7,f6,241*f4,e4,74,e4,10*f4,f7,f6,254*f4,f7,f6,254*f4,f7
  //   ,f6,254*f4,f7,f6,254*f4,f7,f6,254*f4,f7,f6,337*f4,8*d8,8*d0,136*f4
  //   ,d8,f4,6*d8,f4,b4,f4,f0,f8,f4,74,b4,f4,f4,f4,d0,f4,f7,f6,241*f4
  //   ,e4,74,e4,10*f4,f7,f6,254*f4,f7,f6,254*f4,f7,f6,254*f4,f7,f6,254*f4
  //   ,f7,f6,254*f4,f7,f6,337*f4,8*d8,8*d0,136*f4,d8,f4,6*d8,f4,b4,f4
  //   ,f0,f8,f4,74,b4,f4,f4,f4,d0,f4,f7,f6,241*f4,e4,74,e4,10*f4,f7
  //   ,f6,254*f4,f7,f6,254*f4,f7,f6,254*f4,f7,f6,254*f4,f7,f6,254*f4
  //   ,f7,f6,337*f4,8*d8,8*d0,136*f4,d8,f4,6*d8,f4,b4,f4,f0,f8,f4,74
  //   ,b4,f4,f4,f4,d0,f4,f7,f6,241*f4,e4,74,e4,10*f4,f7,f6,254*f4,f7
  //   ,f6,254*f4,f7,f6,254*f4,f7,f6,254*f4,f7,f6,254*f4,f7,f6,337*f4
  //   ,8*d8,8*d0,136*f4,d8,f4,6*d8,f4,b4,f4,f0,f8,f4,74,b4,f4,f4,f4
  //   ,d0,f4,f7,f6,241*f4,e4,74,e4,10*f4,f7,f6,254*f4,f7,f6,254*f4,f7
  //   ,f6,254*f4,f7,f6,254*f4,f7,f6,254*f4,f7,f6,337*f4,8*d8,8*d0,136*f4
  //   ,d8,f4,6*d8,f4,b4,f4,f0,f8,f4,74,b4,f4,f4,f4,d0,f4,f7,f6,241*f4
  //   ,e4,74,e4,10*f4,f7,f6,254*f4,f7,f6,254*f4,f7,f6,254*f4,f7,f6,254*f4
  //   ,f7,f6,254*f4,f7,f6,337*f4,8*d8,8*d0,136*f4,d8,f4,6*d8,f4,b4,f4
  //   ,f0,f8,f4,74,b4,f4,f4,f4,d0,f4,f7,f6,241*f4,e4,74,e4,10*f4,f7
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endmodule
