// Digital circuit MAR.dig as structural Verilog
module MAR (
  input  [7:0] D_BUS,
  input  nMAR_OE,
  input  nMARL_LD,
  input  nMARH_LD,
  input  RST,
  input  CLK,
  output [15:0] A_BUS
);

  _74173 _74173_1 (
    .pin1(nMAR_OE), .pin2(nMAR_OE), .pin3(A_BUS[15]), .pin4(A_BUS[14]), .pin5(A_BUS[13]), .pin6(A_BUS[12]),
    .pin7(CLK), .pin8(1'b0), .pin9(nMARH_LD), .pin10(nMARH_LD), .pin11(D_BUS[4]), .pin12(D_BUS[5]),
    .pin13(D_BUS[6]), .pin14(D_BUS[7]), .pin15(RST), .pin16(1'b1));
  _74173 _74173_2 (
    .pin1(nMAR_OE), .pin2(nMAR_OE), .pin3(A_BUS[11]), .pin4(A_BUS[10]), .pin5(A_BUS[9]), .pin6(A_BUS[8]),
    .pin7(CLK), .pin8(1'b0), .pin9(nMARH_LD), .pin10(nMARH_LD), .pin11(D_BUS[0]), .pin12(D_BUS[1]),
    .pin13(D_BUS[2]), .pin14(D_BUS[3]), .pin15(RST), .pin16(1'b1));
  _74173 _74173_3 (
    .pin1(nMAR_OE), .pin2(nMAR_OE), .pin3(A_BUS[7]), .pin4(A_BUS[6]), .pin5(A_BUS[5]), .pin6(A_BUS[4]),
    .pin7(CLK), .pin8(1'b0), .pin9(nMARL_LD), .pin10(nMARL_LD), .pin11(D_BUS[4]), .pin12(D_BUS[5]),
    .pin13(D_BUS[6]), .pin14(D_BUS[7]), .pin15(RST), .pin16(1'b1));
  _74173 _74173_4 (
    .pin1(nMAR_OE), .pin2(nMAR_OE), .pin3(A_BUS[3]), .pin4(A_BUS[2]), .pin5(A_BUS[1]), .pin6(A_BUS[0]),
    .pin7(CLK), .pin8(1'b0), .pin9(nMARL_LD), .pin10(nMARL_LD), .pin11(D_BUS[0]), .pin12(D_BUS[1]),
    .pin13(D_BUS[2]), .pin14(D_BUS[3]), .pin15(RST), .pin16(1'b1));

  // Other names for the same wires on the sheet: MAR_OE = nMAR_OE; MARH_LD = nMARH_LD; MARL_LD = nMARL_LD
endmodule
